# Fritzing sketch led (saved by Fritzing 0.9.3b)
breadboards: 1

parts:
  Part1 = Bluetooth HC-05 Macho
  LED1 = LED - 3mm [color="Red (633nm)" package="3 mm [THT]"]
  R1 = Resistor [tolerance=±5% resistance=220 package=THT]
  Part3 = Arduino Uno (Rev3) - ICSP

nets:
  N1: Part1.TXD, Part3.D0/RX
  N2: Part1.RXD, Part3.D1/TX
  VCC: Part1.VCC, Part3.5V
  GND: Part1.GND, Part3.GND
  N3: LED1.anode, R1.Pin_0
  N4: R1.Pin_1, Part3.D9_PWM
